# Fritzing sketch Fritzing (saved by Fritzing 0.9.3b)
breadboards: 1

parts:
  MotorSheild = Arduino Motor Shield (Rev3)
  LCD = LCD-16X2 [package=lcd-8x2-kit]
  M1 = DC Motor
  J1 = Basic Servo
  OpticalSensor1 = PHOTOTRANSISTOR REFLECTIVE OBJECT SENSOR [package=qrb1114-side]
  VCC1 = 4 x AAA Battery Mount
  M2 = DC Motor
  hc-sr1 = hc-sr04
  T1 = LM35 Temperature Sensor [package="TO92 [THT]"]
  Shift2 = 74HC595 [package="DIP16 [THT]"]
  R8 = Resistor [tolerance=±5% resistance=1k package=THT]
  C1 = Ceramic Capacitor [capacitance=100nF package="100 mil [THT, multilayer]"]
  R9 = Resistor [tolerance=±5% resistance=5.1k package=THT]
  Pot1 = POT [package=pot_alpha_rv16af-20]
  R10 = Resistor [tolerance=±5% resistance=100 package=THT]
  R11 = Resistor [tolerance=±5% resistance=5.1k package=THT]
  OpticalSensor2 = PHOTOTRANSISTOR REFLECTIVE OBJECT SENSOR [package=qrb1114-side]
  R12 = Resistor [tolerance=±5% resistance=100 package=THT]
  OpticalSensor4 = PHOTOTRANSISTOR REFLECTIVE OBJECT SENSOR [package=qrb1114-side]
  R16 = Resistor [tolerance=±5% resistance=100 package=THT]
  R17 = Resistor [tolerance=±5% resistance=5.1k package=THT]
  HallEffectSensor1 = US5881 [package=to-92-kit]
  C2 = Ceramic Capacitor [capacitance=100nF package="100 mil [THT, multilayer]"]
  C3 = Ceramic Capacitor [capacitance=100nF package="100 mil [THT, multilayer]"]
  R18 = Resistor [tolerance=±5% resistance=10k package=THT]
  HallEffectSensor2 = US5881 [package=to-92-kit]
  C4 = Ceramic Capacitor [capacitance=100nF package="100 mil [THT, multilayer]"]
  C5 = Ceramic Capacitor [capacitance=100nF package="100 mil [THT, multilayer]"]
  R19 = Resistor [tolerance=±5% resistance=10k package=THT]
  C7 = Ceramic Capacitor [capacitance=100nF package="100 mil [THT, multilayer]"]
  J2 = Basic Servo
  SW2 = DIP SWITCH [package=dipswitch-02]
  C9 = Ceramic Capacitor [capacitance=100nF package="100 mil [THT, multilayer]"]
  OpticalSensor3 = PHOTOTRANSISTOR REFLECTIVE OBJECT SENSOR [package=qrb1114-side]
  R14 = Resistor [tolerance=±5% resistance=100 package=THT]
  R15 = Resistor [tolerance=±5% resistance=5.1k package=THT]
  R13 = Resistor [tolerance=±5% resistance=5.1k package=THT]
  Shift3 = 74HC595 [package="DIP16 [THT]"]
  D1 = Zener Diode [part_number=1N4732A breakdown_voltage=3.6V package="Melf DO-213 AB [SMD]"]
  D2 = Zener Diode [part_number=1N4732A breakdown_voltage=3.6V package="Melf DO-213 AB [SMD]"]
  D3 = Zener Diode [part_number=1N4732A breakdown_voltage=3.6V package="Melf DO-213 AB [SMD]"]
  D4 = Zener Diode [part_number=1N4732A breakdown_voltage=3.6V package="Melf DO-213 AB [SMD]"]
  D5 = Zener Diode [part_number=1N4732A breakdown_voltage=3.6V package="Melf DO-213 AB [SMD]"]
  D6 = Zener Diode [part_number=1N4732A breakdown_voltage=3.6V package="Melf DO-213 AB [SMD]"]
  SW3 = DIP SWITCH [package=dipswitch-02]
  LED1 = LED - 3mm [color="Red (633nm)" package="3 mm [THT]"]
  LED2 = LED - 3mm [color="Green (565nm)" package="3 mm [THT]"]
  R20 = Resistor [tolerance=±5% resistance=220 package=THT]
  R21 = Resistor [tolerance=±5% resistance=220 package=THT]
  J3 = Piezo Speaker
  S1 = Pushbutton [package=THT]
  S2 = Pushbutton [package=THT]

nets:
  N1: MotorSheild.A0, T1.Vout
  N2: MotorSheild.A1, OpticalSensor3.C, R15.Pin_1
  N3: MotorSheild.A2, OpticalSensor4.C, R17.Pin_1
  N4: MotorSheild.A3, OpticalSensor2.C, R13.Pin_1
  N5: MotorSheild.A4, OpticalSensor1.C, R11.Pin_1
  N6: MotorSheild.A5, HallEffectSensor1.VOUT, C2.1, R18.Pin_1
  N7: MotorSheild.D8/BreakeB, hc-sr1.Echo
  N8: MotorSheild.D9/BreakeA, MotorSheild.D13/DirB, Shift2.DS
  N9: MotorSheild.D10_PWM, J2.pulse
  N10: MotorSheild.D11_PWM/B, J1.pulse
  N11: MotorSheild.D12/DirA, Shift2.ST_CP, Shift3.ST_CP
  GND: MotorSheild.GND, LCD.VSS, LCD.R_W, LCD.K, J1.gnd, OpticalSensor1.E, OpticalSensor1.K, VCC1.-, hc-sr1.GND, T1.GND, Shift2.GND, Shift2.OE, R8.Pin_0, C1.1, Pot1.E, OpticalSensor2.E, OpticalSensor2.K, OpticalSensor4.E, OpticalSensor4.K, HallEffectSensor1.GND, C2.0, C3.1, HallEffectSensor2.GND, C4.0, C5.0, C7.0, J2.gnd, C9.0, OpticalSensor3.E, OpticalSensor3.K, Shift3.GND, Shift3.OE, R20.Pin_0, R21.Pin_0, J3.pin1
  N12: MotorSheild.D2, R8.Pin_1, C1.0, SW2.3, SW2.4, SW3.3, SW3.4, S1.leg0, S2.leg0
  VCC: MotorSheild.D3_PWM/A, MotorSheild.5V, LCD.VDD, J1.vcc, hc-sr1.VCC, T1.+Vs, Shift2.MR, Shift2.VCC, R9.Pin_1, Pot1.A, R10.Pin_0, R11.Pin_0, R17.Pin_0, HallEffectSensor1.VCC, C3.0, R18.Pin_0, HallEffectSensor2.VCC, HallEffectSensor2.VOUT, C4.1, C5.1, R19.Pin_0, R19.Pin_1, C7.1, J2.vcc, C9.1, R15.Pin_0, R13.Pin_0, Shift3.MR, Shift3.VCC
  N13: MotorSheild.B-, M1.pin_2
  N14: MotorSheild.B+, M1.pin_1
  N15: MotorSheild.A-, M2.pin_2
  N16: MotorSheild.A+, M2.pin_1
  N17: MotorSheild.VMOT, VCC1.+
  N18: LCD.VO, Pot1.S
  N19: LCD.RS, Shift2.Q1
  N20: LCD.E, Shift2.Q2
  N21: LCD.DB4, Shift2.Q3
  N22: LCD.DB5, Shift2.Q4
  N23: LCD.DB6, Shift2.Q5
  N24: LCD.DB7, Shift2.Q6
  N25: LCD.A, R9.Pin_0
  N26: OpticalSensor1.A, R10.Pin_1
  N27: hc-sr1.Trig, Shift2.Q0
  N28: Shift2.Q7, J3.pin2
  N29: Shift2.Q7', Shift3.DS
  N30: Shift2.SH_CP, Shift3.SH_CP
  N31: OpticalSensor2.A, R12.Pin_1
  N32: OpticalSensor4.A, R16.Pin_1
  N33: SW2.1, D2.cathode
  N34: SW2.2, D5.cathode
  N35: OpticalSensor3.A, R14.Pin_1
  N36: Shift3.Q1, LED2.anode
  N37: Shift3.Q2, D4.anode
  N38: Shift3.Q3, D1.anode
  N39: Shift3.Q4, D3.anode
  N40: Shift3.Q5, D2.anode
  N41: Shift3.Q6, D5.anode
  N42: Shift3.Q7, D6.anode
  N43: Shift3.Q0, LED1.anode
  N44: D1.cathode, SW3.1
  N45: D3.cathode, SW3.2
  N46: D4.cathode, S1.leg1
  N47: LED1.cathode, R21.Pin_1
  N48: LED2.cathode, R20.Pin_1

notes:
  These two pushbuttons are actually lever switches
  One servo motor is used to turn the ultrasonic sensor, and the other one is used in our additinal functinality to movce the pen

custom parts:
  US5881: Precision degC temp sensor, analog out
