# Fritzing sketch P1 _PR1_Circuit (saved by Fritzing 0.9.3b)
breadboards: 1

parts:
  hc-sr1 = hc-sr04
  T1 = LM35 Temperature Sensor [package="TO92 [THT]"]
  J1 = Basic Servo
  Q1 = PNP-Transistor [package="TO92 [THT]"]
  Q2 = PNP-Transistor [package="TO92 [THT]"]
  M1 = DC Motor
  Part2 = Arduino Motor Shield (Rev3)
  M2 = DC Motor
  VCC1 = Battery
  C1 = Capacitor [package=cap-pth-small]
  R1 = Resistor [tolerance=±5% resistance=220 package="2010 [SMD]"]
  C2 = Ceramic Capacitor [capacitance="100 nF" package="0603 [SMD, multilayer]"]
  C3 = Ceramic Capacitor [capacitance="100 nF" package="0603 [SMD, multilayer]"]
  C4 = Ceramic Capacitor [capacitance="100 nF" package="0603 [SMD, multilayer]"]
  R2 = Resistor [tolerance=±5% resistance=220 package="2010 [SMD]"]

nets:
  VCC: hc-sr1.VCC, T1.+Vs, J1.vcc, J1.pulse, Q1.E, Q2.E, Part2.D10_PWM, Part2.5V, C1.1, R1.Pin_1, C2.0, C2.1, C4.1, R2.Pin_1
  N1: hc-sr1.Trig, Part2.SCL
  N2: hc-sr1.Echo, Part2.SDA
  GND: hc-sr1.GND, T1.GND, J1.gnd, Q1.C, Q2.C, Part2.GND, VCC1.-, C3.0, C4.0
  N3: T1.Vout, Part2.A0
  N4: Q1.B, Part2.D2, C1.2, R1.Pin_0
  N5: Q2.B, Part2.D8/BreakeB, C3.1, R2.Pin_0
  N6: M1.pin_1, Part2.A+
  N7: M1.pin_2, Part2.A-
  N8: Part2.B-, M2.pin_2
  N9: Part2.B+, M2.pin_1
  N10: Part2.VMOT, VCC1.+

notes:
  Hall Effect Sensors - Pins D2, D8
  Note: Hall Effect Sensor not in Library, substituted with PNP Transistor Schematics
  URF TRIG - SCL Pin
  URF EDGE - SDA Pin
  Servo - Pin D10
  LM35 - Pin A0
