# Fritzing sketch project1 (saved by Fritzing 0.9.3b)
breadboards: 1

parts:
  MotorSheild = Arduino Motor Shield (Rev3)
  LCD = LCD-16X2 [package=lcd-8x2-kit]
  Q1 = NPN-Transistor [part_number=2N3904 package="TO92 [THT]"]
  M1 = DC Motor
  J1 = Basic Servo
  Shift1 = 74HC595 [package="DIP16 [THT]"]
  OpticalSensor1 = PHOTOTRANSISTOR REFLECTIVE OBJECT SENSOR [package=qrb1114-side]
  VCC1 = 4 x AAA Battery Mount
  M2 = DC Motor
  hc-sr1 = hc-sr04
  T1 = LM35 Temperature Sensor [package="TO92 [THT]"]
  Shift2 = 74HC595 [package="DIP16 [THT]"]
  Shift3 = 74HC595 [package="DIP16 [THT]"]
  D2 = Rectifier Diode [part_number=1N4007 package="300 mil [THT]"]
  D3 = Rectifier Diode [part_number=1N4007 package="300 mil [THT]"]
  D4 = Rectifier Diode [part_number=1N4007 package="300 mil [THT]"]
  D5 = Rectifier Diode [part_number=1N4007 package="300 mil [THT]"]
  D0 = Rectifier Diode [part_number=1N4007 package="300 mil [THT]"]
  R1 = Resistor [tolerance=±5% resistance=5.1k package=THT]
  Q2 = NPN-Transistor [part_number=2N3904 package="TO92 [THT]"]
  R2 = Resistor [tolerance=±5% resistance=5.1k package=THT]
  Q3 = NPN-Transistor [part_number=2N3904 package="TO92 [THT]"]
  R3 = Resistor [tolerance=±5% resistance=5.1k package=THT]
  Q4 = NPN-Transistor [part_number=2N3904 package="TO92 [THT]"]
  R4 = Resistor [tolerance=±5% resistance=5.1k package=THT]
  Q5 = NPN-Transistor [part_number=2N3904 package="TO92 [THT]"]
  R5 = Resistor [tolerance=±5% resistance=5.1k package=THT]
  R8 = Resistor [tolerance=±5% resistance=1k package=THT]
  C1 = Ceramic Capacitor [capacitance=100nF package="100 mil [THT, multilayer]"]
  R9 = Resistor [tolerance=±5% resistance=5.1k package=THT]
  Pot1 = POT [package=pot_alpha_rv16af-20]
  R10 = Resistor [tolerance=±5% resistance=100 package=THT]
  R11 = Resistor [tolerance=±5% resistance=5.1k package=THT]
  OpticalSensor2 = PHOTOTRANSISTOR REFLECTIVE OBJECT SENSOR [package=qrb1114-side]
  R12 = Resistor [tolerance=±5% resistance=100 package=THT]
  OpticalSensor4 = PHOTOTRANSISTOR REFLECTIVE OBJECT SENSOR [package=qrb1114-side]
  R16 = Resistor [tolerance=±5% resistance=100 package=THT]
  R17 = Resistor [tolerance=±5% resistance=5.1k package=THT]
  HallEffectSensor1 = US5881 [package=to-92-kit]
  C2 = Ceramic Capacitor [capacitance=100nF package="100 mil [THT, multilayer]"]
  C3 = Ceramic Capacitor [capacitance=100nF package="100 mil [THT, multilayer]"]
  R18 = Resistor [tolerance=±5% resistance=10k package=THT]
  HallEffectSensor2 = US5881 [package=to-92-kit]
  C4 = Ceramic Capacitor [capacitance=100nF package="100 mil [THT, multilayer]"]
  C5 = Ceramic Capacitor [capacitance=100nF package="100 mil [THT, multilayer]"]
  R19 = Resistor [tolerance=±5% resistance=10k package=THT]
  C7 = Ceramic Capacitor [capacitance=100nF package="100 mil [THT, multilayer]"]
  J2 = Basic Servo
  D7 = Rectifier Diode [part_number=1N4007 package="300 mil [THT]"]
  Q6 = NPN-Transistor [part_number=2N3904 package="TO92 [THT]"]
  R6 = Resistor [tolerance=±5% resistance=5.1k package=THT]
  SW2 = DIP SWITCH [package=dipswitch-02]
  C9 = Ceramic Capacitor [capacitance=100nF package="100 mil [THT, multilayer]"]
  OpticalSensor3 = PHOTOTRANSISTOR REFLECTIVE OBJECT SENSOR [package=qrb1114-side]
  R14 = Resistor [tolerance=±5% resistance=100 package=THT]
  R15 = Resistor [tolerance=±5% resistance=5.1k package=THT]
  R13 = Resistor [tolerance=±5% resistance=5.1k package=THT]
  D8 = Rectifier Diode [part_number=1N4007 package="300 mil [THT]"]
  D9 = Rectifier Diode [part_number=1N4007 package="300 mil [THT]"]

nets:
  N1: MotorSheild.A2, OpticalSensor4.C, R17.Pin_1
  N2: MotorSheild.A3, OpticalSensor2.C, R13.Pin_1
  N3: MotorSheild.A0, T1.Vout
  N4: MotorSheild.A1, OpticalSensor3.C, R15.Pin_1
  N5: MotorSheild.A4, OpticalSensor1.C, R11.Pin_1
  N6: MotorSheild.A5, Q1.E, Q2.E, Q3.E, Q4.E, Q5.E, R8.Pin_1, C1.0, Q6.E, SW2.3, SW2.4
  N7: MotorSheild.D8/BreakeB, hc-sr1.Echo
  N8: MotorSheild.D9/BreakeA, Shift1.SH_CP, Shift2.SH_CP, Shift3.SH_CP
  N9: MotorSheild.D10_PWM, J2.pulse
  N10: MotorSheild.D11_PWM/B, J1.pulse
  N11: MotorSheild.D12/DirA, Shift1.ST_CP, Shift2.ST_CP, Shift3.ST_CP
  N12: MotorSheild.D13/DirB, Shift1.DS
  GND: MotorSheild.GND, LCD.VSS, LCD.R_W, LCD.K, J1.gnd, Shift1.GND, Shift1.OE, OpticalSensor1.E, OpticalSensor1.K, VCC1.-, hc-sr1.GND, T1.GND, Shift2.GND, Shift2.OE, Shift3.GND, Shift3.OE, R8.Pin_0, C1.1, Pot1.E, OpticalSensor2.E, OpticalSensor2.K, OpticalSensor4.E, OpticalSensor4.K, HallEffectSensor1.GND, C2.0, C3.1, HallEffectSensor2.GND, C4.0, C5.0, C7.0, J2.gnd, C9.0, OpticalSensor3.E, OpticalSensor3.K
  N13: MotorSheild.D2, HallEffectSensor1.VOUT, C2.1, R18.Pin_1
  VCC: MotorSheild.D3_PWM/A, MotorSheild.5V, LCD.VDD, J1.vcc, Shift1.MR, Shift1.VCC, hc-sr1.VCC, T1.+Vs, Shift2.MR, Shift2.VCC, Shift3.MR, Shift3.VCC, R9.Pin_1, Pot1.A, R10.Pin_0, R11.Pin_0, R17.Pin_0, HallEffectSensor1.VCC, C3.0, R18.Pin_0, HallEffectSensor2.VCC, HallEffectSensor2.VOUT, C4.1, C5.1, R19.Pin_0, R19.Pin_1, C7.1, J2.vcc, C9.1, R15.Pin_0, R13.Pin_0
  N14: MotorSheild.B-, M1.pin_2
  N15: MotorSheild.B+, M1.pin_1
  N16: MotorSheild.A-, M2.pin_2
  N17: MotorSheild.A+, M2.pin_1
  N18: MotorSheild.VMOT, VCC1.+
  N19: LCD.VO, Pot1.S
  N20: LCD.RS, Shift2.Q1
  N21: LCD.E, Shift2.Q2
  N22: LCD.DB4, Shift2.Q3
  N23: LCD.DB5, Shift2.Q4
  N24: LCD.DB6, Shift2.Q5
  N25: LCD.DB7, Shift2.Q6
  N26: LCD.A, R9.Pin_0
  N27: Q1.B, R1.Pin_1
  N28: Q1.C, D7.cathode
  N29: Shift1.Q7', Shift2.DS
  N30: OpticalSensor1.A, R10.Pin_1
  N31: hc-sr1.Trig, Shift2.Q0
  N32: Shift2.Q7', Shift3.DS
  N33: Shift3.Q1, D2.anode
  N34: Shift3.Q2, D3.anode
  N35: Shift3.Q3, D5.anode
  N36: Shift3.Q4, D0.anode
  N37: Shift3.Q5, D4.anode
  N38: Shift3.Q6, D8.anode
  N39: Shift3.Q7, D9.anode
  N40: Shift3.Q0, D7.anode
  N41: D2.cathode, Q6.C
  N42: D3.cathode, Q3.C
  N43: D4.cathode, Q5.C
  N44: D5.cathode, Q2.C
  N45: D0.cathode, Q4.C
  N46: Q2.B, R2.Pin_0, R2.Pin_1
  N47: Q3.B, R3.Pin_0, R3.Pin_1
  N48: Q4.B, R4.Pin_0, R4.Pin_1
  N49: Q5.B, R5.Pin_0, R5.Pin_1
  N50: OpticalSensor2.A, R12.Pin_1
  N51: OpticalSensor4.A, R16.Pin_1
  N52: Q6.B, R6.Pin_0, R6.Pin_1
  N53: SW2.1, D8.cathode
  N54: SW2.2, D9.cathode
  N55: OpticalSensor3.A, R14.Pin_1

custom parts:
  US5881: Precision degC temp sensor, analog out
